// Digital circuit CG-16-1-Processor.dig as structural Verilog
module CG_16_1_Processor (
  input  clk,
  input  in_2,
  input  [15:0] in_3,
  input  in_4,
  input  in_5,
  input  in_6,
  input  in_7,
  input  in_8,
  input  in_9,
  input  in_10,
  input  in_11,
  input  in_12,
  input  in_13,
  input  in_14,
  input  in_15,
  input  in_16,
  input  in_17,
  input  in_18,
  input  in_19,
  input  in_20,
  input  in_21,
  input  in_22,
  input  in_23,
  input  in_24,
  input  in_25,
  input  in_26,
  input  in_27,
  input  in_28,
  input  in_29,
  input  in_30,
  input  in_31,
  input  in_32,
  input  [4:0] in_33,
  input  in_34,
  input  in_35,
  input  in_36,
  input  in_37,
  input  in_38,
  input  in_39,
  input  in_40,
  input  in_41,
  input  in_42,
  input  in_43,
  input  in_44,
  input  in_45,
  input  in_46,
  input  in_47,
  input  in_48
);

  wire and_1_out, and_2_out, and_3_out, and_4_out, and_5_out, carry, carryclear, carryset, equalclear,
       equalset, Gr_RAM_check_eq, lessthanclear, lessthanset, morethanclear, morethanset, negativeclear,
       negativeset, Page_Select_q, Program_Counter_ovf, ROM_check_eq, zeroclear, zeroset;
  wire [6:1] Zero_Flag_q;
  wire [7:0] address_bus, Program_Counter_Bank_Select_out;
  wire [11:0] cg_16_1_alu_1_c_out;
  wire [15:0] accumulator, address, blockramdualport_1_d, bus, Instruction_Register_q, Program_Counter_out,
       Stack_Base_Pointer_q, Stack_Top_Pointer_q, X_q, Y_q, Z_q;

  Register #(.Bits(16)) X (.D(bus), .C(clk), .en(in_5), .Q(X_q));
  Register #(.Bits(16)) Y (.D(bus), .C(clk), .en(in_11), .Q(Y_q));
  Register #(.Bits(16)) Z (.D(bus), .C(clk), .en(in_13), .Q(Z_q));
  Register #(.Bits(16)) u_Accumulator (.D(bus), .C(clk), .en(in_15), .Q(accumulator));
  CounterPreset #(.Bits(16)) Program_Counter (
    .en(in_20), .C(clk), .dir(1'b0), .in(bus), .ld(in_17), .clr(in_19), .out(Program_Counter_out),
    .ovf(Program_Counter_ovf));
  Register #(.Bits(16)) Instruction_Register (.D(bus), .C(clk), .en(in_24), .Q(Instruction_Register_q));
  Register #(.Bits(16)) Stack_Top_Pointer (.D(bus), .C(clk), .en(in_28), .Q(Stack_Top_Pointer_q));
  Register #(.Bits(16)) Stack_Base_Pointer (.D(bus), .C(clk), .en(in_26), .Q(Stack_Base_Pointer_q));
  Register #(.Bits(8)) Bank_Select_Register (.D(bus[7:0]), .C(clk), .en(in_30), .Q(address_bus));
  Register #(.Bits(16)) Address_Access_Register (.D(bus), .C(clk), .en(in_32), .Q(address));
  assign bus = in_4 ? in_3 : 16'bz;  // Driver driver_1
  assign bus = in_6 ? X_q : 16'bz;  // Driver driver_2
  assign bus = in_12 ? Y_q : 16'bz;  // Driver driver_3
  assign bus = in_14 ? Z_q : 16'bz;  // Driver driver_4
  assign bus = in_16 ? accumulator : 16'bz;  // Driver driver_5
  assign bus = in_18 ? Program_Counter_out : 16'bz;  // Driver driver_6
  CounterPreset #(.Bits(8)) Program_Counter_Bank_Select (
    .en(Program_Counter_ovf), .C(clk), .dir(1'b0), .in(bus[7:0]), .ld(in_23), .clr(in_22),
    .out(Program_Counter_Bank_Select_out));  // open: ovf
  assign bus = in_25 ? Instruction_Register_q : 16'bz;  // Driver driver_7
  assign bus = in_29 ? Stack_Top_Pointer_q : 16'bz;  // Driver driver_8
  assign bus = in_27 ? Stack_Base_Pointer_q : 16'bz;  // Driver driver_9
  assign bus = in_31 ? {{8{1'b0}}, address_bus} : 16'bz;  // Driver driver_10
  assign bus = in_21 ? {{8{1'b0}}, Program_Counter_Bank_Select_out} : 16'bz;  // Driver driver_11
  CG_16_1_ALU cg_16_1_alu_1 (
    .OP(in_33), .A(accumulator), .B(bus), .C_in(carry), .C_out(cg_16_1_alu_1_c_out[0]),
    .Z(cg_16_1_alu_1_c_out[2]), .N(cg_16_1_alu_1_c_out[4]), .A_gt_B(cg_16_1_alu_1_c_out[6]),
    .A_eq_B(cg_16_1_alu_1_c_out[8]), .A_lt_B(cg_16_1_alu_1_c_out[10]));  // open: X, X_high
  not not_1 (cg_16_1_alu_1_c_out[1], cg_16_1_alu_1_c_out[0]);
  not not_2 (cg_16_1_alu_1_c_out[3], cg_16_1_alu_1_c_out[2]);
  not not_3 (cg_16_1_alu_1_c_out[5], cg_16_1_alu_1_c_out[4]);
  not not_4 (cg_16_1_alu_1_c_out[7], cg_16_1_alu_1_c_out[6]);
  not not_5 (cg_16_1_alu_1_c_out[9], cg_16_1_alu_1_c_out[8]);
  not not_6 (cg_16_1_alu_1_c_out[11], cg_16_1_alu_1_c_out[10]);
  Multiplexer #(.Bits(12)) multiplexer_1 (
    .sel(in_34), .in_0({in_46, in_45, in_44, in_43, in_42, in_41, in_40, in_39, in_38, in_37, in_36, in_35}),
    .in_1(cg_16_1_alu_1_c_out),
    .out({lessthanclear, lessthanset, equalclear, equalset, morethanclear, morethanset, negativeclear, negativeset, zeroclear, zeroset, carryclear, carryset}));
  RS_FF Carry_Flag (.S(carryset), .C(clk), .R(carryclear), .Q(carry));  // open: nQ
  RS_FF Zero_Flag (.S(zeroset), .C(clk), .R(zeroclear), .Q(Zero_Flag_q[1]));  // open: nQ
  RS_FF Negative_Flag (.S(negativeset), .C(clk), .R(negativeclear), .Q(Zero_Flag_q[2]));  // open: nQ
  RS_FF More_Than_Flag (.S(morethanset), .C(clk), .R(morethanclear), .Q(Zero_Flag_q[3]));  // open: nQ
  RS_FF Equal_Flag (.S(equalset), .C(clk), .R(equalclear), .Q(Zero_Flag_q[4]));  // open: nQ
  RS_FF Less_Than_Flag (.S(lessthanset), .C(clk), .R(lessthanclear), .Q(Zero_Flag_q[5]));  // open: nQ
  RS_FF Interrupt_Disable_Flag (.S(in_47), .C(clk), .R(in_48), .Q(Zero_Flag_q[6]));  // open: nQ
  assign bus = in_2 ? {{9{1'b0}}, Zero_Flag_q, carry} : 16'bz;  // Driver driver_12
  LED u_Carry (.in(carry));
  LED Zero (.in(Zero_Flag_q[1]));
  LED Negative (.in(Zero_Flag_q[2]));
  LED More_Than (.in(Zero_Flag_q[3]));
  LED Equal (.in(Zero_Flag_q[4]));
  LED Less_Than (.in(Zero_Flag_q[5]));
  LED Interrupt_Disable (.in(Zero_Flag_q[6]));
  Comparator #(.Bits(8)) Gr_RAM_check (.a(address_bus), .b({8{1'b1}}), .eq(Gr_RAM_check_eq));  // open: gt, lt
  Comparator #(.Bits(8)) ROM_check (.a(address_bus), .b({8{1'b0}}), .eq(ROM_check_eq));  // open: gt, lt
  and and_1 (and_1_out, Gr_RAM_check_eq, in_10);
  and and_2 (and_2_out, ROM_check_eq, in_10);
  and and_3 (and_3_out, ~Gr_RAM_check_eq, in_9);  // And
  and and_4 (and_4_out, in_9, Gr_RAM_check_eq);
  RS_FF Page_Select (.S(in_8), .C(clk), .R(in_7), .Q(Page_Select_q));  // open: nQ
  ROM #(.AddrBits(16), .Bits(16)) rom_1 (.A(address), .sel(and_2_out), .D(bus));
  BlockRAMDualPort #(.AddrBits(24), .Bits(16)) blockramdualport_1 (
    .A({address_bus, address}), .Din(bus), .str(and_3_out), .C(clk), .D(blockramdualport_1_d));
  GraphicCard #(.graphicHeight(160), .Bits(16), .graphicWidth(200)) graphiccard_1 (
    .A(address), .str(and_4_out), .C(clk), .ld(and_1_out), .B(Page_Select_q), .D(bus));
  and and_5 (and_5_out, in_10, ~Gr_RAM_check_eq);  // And
  assign bus = and_5_out ? blockramdualport_1_d : 16'bz;  // Driver driver_13

  // Other names for the same wires on the sheet: aawrite = in_32; aluop[4:0] = in_33; aluwriteflags = in_34;
  //   aread = in_16; awrite = in_15; bsread = in_31; bswrite = in_30; clock = clk; disableinterrupts = in_47;
  //   enableinterrupts = in_48; irread = in_25; irwrite = in_24; mmuread = in_10; mmuwrite = in_9; pcbsclr = in_22;
  //   pcbsread = in_21; pcbswrite = in_23; pcclr = in_19; pcinc = in_20; pcread = in_18; pcwrite = in_17;
  //   sbread = in_27; sbwrite = in_26; stread = in_29; stwrite = in_28; xread = in_6; xwrite = in_5; yread = in_12;
  //   ywrite = in_11; zread = in_14; zwrite = in_13

  // Notes on the sheet:
  //   Registers
  //   Control Logic
  //   ALU
  //   Flags
  //   MMU
endmodule
